# Fritzing sketch rpi_pico_w_wiring_diagram (saved by Fritzing 0.9.6b)
breadboards: 1

parts:
  Mod1 = Raspberry Pi Pico W
  J2 = Basic Servo
  Part2 = Real Time Clock Module - DS1307 RTC Breakout Board [part_number="RTC module"]
  S2 = Round Pushbutton

nets:
  GND: Mod1.pin_18, Mod1.pin_23, Mod1.pin_38, J2.gnd, Part2.GND, S2.leg0
  N1: Mod1.pin_21, Part2.SDA
  N2: Mod1.pin_22, Part2.SCL
  N3: Mod1.pin_26, S2.leg1
  N4: Mod1.pin_27, J2.pulse
  VCC: Mod1.pin_40, J2.vcc, Part2.5V

custom parts:
  Raspberry Pi Pico W: Raspberry Pi Pico W. Based around the RP2040 microcontroller the Pico W is a low cost microcontroller device bringing Raspberry Pi quality, cost, and easy of use to the microcontroller space. The areas marked KEEPOUT in pcb silkscreen should not have traces running through them to avoid shorts on a soldered in module!
